# Fritzing sketch 16-11-2017 (saved by Fritzing 0.9.3b)
breadboards: 1

parts:
  Part1 = Arduino Uno (Rev3) - ICSP
  S1 = Pushbutton [package="[THT]"]
  S2 = Pushbutton [package="[THT]"]
  S3 = Pushbutton [package="[THT]"]
  S4 = Pushbutton [package="[THT]"]
  LED5 = smd LED [color="Red (633nm)" package="1206 [SMD]"]
  LED6 = smd LED [color="Red (633nm)" package="1206 [SMD]"]
  LED7 = smd LED [color="Red (633nm)" package="1206 [SMD]"]
  LED8 = smd LED [color="Red (633nm)" package="1206 [SMD]"]
  R1 = Resistor [tolerance=±5% resistance=220 package="2010 [SMD]"]
  R2 = Resistor [tolerance=±5% resistance=220 package="2010 [SMD]"]
  R3 = Resistor [tolerance=±5% resistance=220 package="2010 [SMD]"]
  R4 = Resistor [tolerance=±5% resistance=220 package="2010 [SMD]"]

nets:
  N1: Part1.D9_PWM, S1.Pin_4
  N2: Part1.D10_PWM/SS, S2.Pin_3, S2.Pin_4
  N3: Part1.D11_PWM/MOSI, S3.Pin_4
  N4: Part1.D12/MISO, LED7.anode
  N5: Part1.D13/SCK, LED8.anode
  N6: Part1.GND, S1.Pin_2, S2.Pin_1, S2.Pin_2, S3.Pin_1, S3.Pin_2, S4.Pin_1, S4.Pin_2, R1.Pin_1, R2.Pin_1, R3.Pin_1, R4.Pin_1
  N7: Part1.D2, LED5.anode
  N8: Part1.D4, LED6.anode
  N9: Part1.D6_PWM, S4.Pin_4
  N10: LED5.cathode, R1.Pin_0
  N11: LED6.cathode, R2.Pin_0
  N12: LED7.cathode, R3.Pin_0
  N13: LED8.cathode, R4.Pin_0
